# Fritzing sketch Multinode_PCB_v3 (saved by Fritzing 0.9.3b)
circuit board: 2.97773cm x 5.12283cm

parts:
  WeMos_D1_Mini = WeMos D1 Mini
  DHT = male pin header, 3 pins [form="♂ (male)"]
  PIR = male pin header, 3 pins [form="♂ (male)"]
  BMx = male pin header, 4 pins [form="♂ (male)"]
  R1 = Resistor [tolerance=±5% resistance=4.7k package=THT]
  SW1 = male pin header, 2 pins [form="♂ (male)"]
  SW2 = male pin header, 2 pins [form="♂ (male)"]
  R2 = Resistor [tolerance=±5% resistance=10k package=THT]
  R3 = Resistor [tolerance=±5% resistance=10k package=THT]
  OLED = male pin header, 4 pins [form="♂ (male)"]

nets:
  3.3V: WeMos_D1_Mini.3V3, DHT.pin3, PIR.pin3, BMx.pin4, R1.Pin_1, R2.Pin_1, R3.Pin_1
  5V: WeMos_D1_Mini.5V, OLED.pin4
  N1: WeMos_D1_Mini.D1, BMx.pin2, OLED.pin2
  N2: WeMos_D1_Mini.D2, BMx.pin3, OLED.pin3
  N3: WeMos_D1_Mini.D3, SW1.pin2, R2.Pin_0
  N4: WeMos_D1_Mini.D4, SW2.pin2, R3.Pin_0
  N5: WeMos_D1_Mini.D7, DHT.pin2, R1.Pin_0
  N6: WeMos_D1_Mini.D8, PIR.pin2
  GND: WeMos_D1_Mini.G, DHT.pin1, PIR.pin1, BMx.pin1, SW1.pin1, SW2.pin1, OLED.pin1

notes:
  J2 = DHT
  J3 = PIR
  J4 = OLED (I2C)
  J5 = Switch
  J6 = Switch
  G
  7
  8
  4
  3
  2
  1
  V
